// Logisim project ALU.circ as structural Verilog: 8 circuits, main circuit main
module main (
  input  [7:0] A,
  input  [7:0] B,
  input  [2:0] sel,
  output [7:0] Out
);

  // Probe on Out
  ALU alu_1 (.A(A), .B(B), .sel(sel), .Out(Out));

  // Notes on the sheet:
  //   Martín Kaliman Schwarz - Gemma Catalano Llamas - Osiris García Parras
  //   Arithmetic Logic Unit - _____ TEAM   
  //   A, B are signed-magnitude numbers
  //   0 -> Outputs A
  //   1 -> Outputs B
  //   2 -> A+B
  //   3 -> A-B
  //   4 -> A*B
  //   5 -> (INT) A/B
  //   6-> A%B
  //   7 -> COMPARISON (A<B -> A ;; ELSE OUTPUT B)
endmodule

module addr (
  input  [7:0] A,
  input  [7:0] B,
  output [7:0] out_3
);

  wire comparator_1_gt, xor_1_out;
  wire [6:0] adder_1_out, multiplexer_1_out, multiplexer_2_out, subtractor_1_out;

  Adder #(.width(7)) adder_1 (.a(A[6:0]), .b(B[6:0]), .out(adder_1_out));  // open: cin, cout
  Multiplexer #(.width(7)) multiplexer_1 (
    .in0(B[6:0]), .in1(A[6:0]), .out(multiplexer_1_out), .sel(comparator_1_gt), .en(1'b1));
  Comparator #(.width(7), .mode("unsigned")) comparator_1 (
    .a(A[6:0]), .b(B[6:0]), .gt(comparator_1_gt));  // open: eq, lt
  xor xor_1 (xor_1_out, A[7], B[7]);
  Multiplexer #(.width(7)) multiplexer_2 (
    .in0(A[6:0]), .in1(B[6:0]), .out(multiplexer_2_out), .sel(comparator_1_gt), .en(1'b1));
  Multiplexer multiplexer_3 (.in0(B[7]), .in1(A[7]), .out(out_3[7]), .sel(comparator_1_gt), .en(1'b1));
  Subtractor #(.width(7)) subtractor_1 (
    .a(multiplexer_1_out), .b(multiplexer_2_out), .out(subtractor_1_out));  // open: bin, bout
  Multiplexer #(.width(7)) multiplexer_4 (
    .in0(adder_1_out), .in1(subtractor_1_out), .out(out_3[6:0]), .sel(xor_1_out), .en(1'b1));

  // Notes on the sheet:
  //   sm_adder - Sebastián de la Torre Gil-Delgado and Osiris García Parras
endmodule

module mult (
  input  [7:0] A,
  input  [7:0] B,
  output [7:0] Out
);

  xor xor_1 (Out[7], A[7], B[7]);
  Multiplier #(.width(7)) multiplier_1 (.a(A[6:0]), .b(B[6:0]), .out(Out[6:0]));  // open: cin, cout
endmodule

module div (
  input  [7:0] A,
  input  [7:0] B,
  output [7:0] Out
);

  wire comparator_1_lt;
  wire [6:0] divider_1_out;
  wire [7:7] xor_1_out;

  xor xor_1 (xor_1_out[7], A[7], B[7]);
  Divider #(.width(7)) divider_1 (.a(A[6:0]), .b(B[6:0]), .out(divider_1_out));  // open: upper, rem
  Comparator #(.width(7), .mode("unsigned")) comparator_1 (
    .a(B[6:0]), .b(7'b0000001), .lt(comparator_1_lt));  // open: gt, eq
  Multiplexer #(.width(8)) multiplexer_1 (
    .in0({xor_1_out[7], divider_1_out}), .in1({8{1'b0}}), .out(Out), .sel(comparator_1_lt));  // open: en
endmodule

module sub (
  input  [7:0] A,
  input  [7:0] B,
  output [7:0] out_3
);

  wire comparator_1_gt, not_1_out, xor_1_out;
  wire [6:0] adder_1_out, multiplexer_1_out, multiplexer_2_out, subtractor_1_out;

  not not_1 (not_1_out, B[7]);
  Adder #(.width(7)) adder_1 (.a(A[6:0]), .b(B[6:0]), .out(adder_1_out));  // open: cin, cout
  Multiplexer #(.width(7)) multiplexer_1 (
    .in0(B[6:0]), .in1(A[6:0]), .out(multiplexer_1_out), .sel(comparator_1_gt), .en(1'b1));
  Comparator #(.width(7), .mode("unsigned")) comparator_1 (
    .a(A[6:0]), .b(B[6:0]), .gt(comparator_1_gt));  // open: eq, lt
  xor xor_1 (xor_1_out, A[7], not_1_out);
  Multiplexer #(.width(7)) multiplexer_2 (
    .in0(A[6:0]), .in1(B[6:0]), .out(multiplexer_2_out), .sel(comparator_1_gt), .en(1'b1));
  Multiplexer multiplexer_3 (.in0(not_1_out), .in1(A[7]), .out(out_3[7]), .sel(comparator_1_gt), .en(1'b1));
  Subtractor #(.width(7)) subtractor_1 (
    .a(multiplexer_1_out), .b(multiplexer_2_out), .out(subtractor_1_out));  // open: bin, bout
  Multiplexer #(.width(7)) multiplexer_4 (
    .in0(adder_1_out), .in1(subtractor_1_out), .out(out_3[6:0]), .sel(xor_1_out), .en(1'b1));

  // Notes on the sheet:
  //   sm_adder - Sebastián de la Torre Gil-Delgado and Osiris García Parras
endmodule

module ALU (
  input  [7:0] A,
  input  [7:0] B,
  input  [2:0] sel,
  output [7:0] Out
);

  wire [7:0] addr_1_out_3, comp_1_out_3, div_1_out, mod_1_out, mult_1_out, sub_1_out_3;

  addr addr_1 (.A(A), .B(B), .out_3(addr_1_out_3));
  sub sub_1 (.A(A), .B(B), .out_3(sub_1_out_3));
  mult mult_1 (.A(A), .B(B), .Out(mult_1_out));
  div div_1 (.A(A), .B(B), .Out(div_1_out));
  mod mod_1 (.A(A), .B(B), .out(mod_1_out));
  comp comp_1 (.A(A), .B(B), .out_3(comp_1_out_3));
  Multiplexer #(.select(3), .width(8)) multiplexer_1 (
    .in0(A), .in1(B), .in2(addr_1_out_3), .in3(sub_1_out_3), .in4(mult_1_out), .in5(div_1_out),
    .in6(mod_1_out), .in7(comp_1_out_3), .out(Out), .sel(sel));  // open: en

  // Notes on the sheet:
  //   Martín Kaliman Schwarz - Gemma Catalano Llamas - Osiris García Parras
  //   Arithmetic Logic Unit - _____ TEAM   
  //   A, B are signed-magnitude numbers
  //   DIVISION BY ZERO BECOMES A 0
  //   OVERFLOW IS UNEXPECTED, UNTREATED BEHAVIOUR
  //   ATTENTION GAMERS!!!! CHECK OUT A-A = -0
endmodule

module mod (
  input  [7:0] A,
  input  [7:0] B,
  output [7:0] out
);

  Divider divider_1 (.a(A), .b(B), .rem(out));  // open: out, upper
endmodule

// cmp
module comp (
  input  [7:0] A,
  input  [7:0] B,
  output [7:0] out_3
);

  wire comparator_1_lt, comparator_2_gt;
  wire [7:0] multiplexer_1_out, multiplexer_2_out;

  Comparator #(.mode("unsigned")) comparator_1 (.a(A), .b(B), .lt(comparator_1_lt));  // open: gt, eq
  Comparator #(.mode("unsigned")) comparator_2 (.a(A), .b(B), .gt(comparator_2_gt));  // open: eq, lt
  Multiplexer #(.width(8)) multiplexer_1 (
    .in0(B), .in1(A), .out(multiplexer_1_out), .sel(comparator_1_lt));  // open: en
  Multiplexer #(.width(8)) multiplexer_2 (
    .in0(B), .in1(A), .out(multiplexer_2_out), .sel(comparator_2_gt));  // open: en
  Multiplexer #(.select(2), .width(8)) multiplexer_3 (
    .in0(multiplexer_1_out), .in1(A), .in2(B), .in3(multiplexer_2_out), .out(out_3), .sel({B[7], A[7]}));  // open: en
endmodule
