// Logisim project Instruction_Memory.circ as structural Verilog: 2 circuits, main circuit main
module main (
  output [15:0] out_1
);

  wire button_1_out, clock_1_out;

  Clock clock_1 (.out(clock_1_out));
  Button button_1 (.out(button_1_out));
  Memory_element memory_element_1 (.Clock(clock_1_out), .Reset(button_1_out), .Current_Instruction(out_1));
  // Probe on out_1

  // Notes on the sheet:
  //   The top left pin is for the clock, the bottom one activates a reset
  //   The output is a 16 bit string, which represent the instruction that is being read
  //   For inputing the instructions, you should change the file that the RAM 
  //   is reading from
endmodule

module Memory_element (
  input  Clock,
  input  Reset,
  output [15:0] Current_Instruction
);

  wire [5:0] adder_1_out, register_1_q;

  Adder #(.width(6)) adder_1 (.a(register_1_q), .b(6'b000001), .out(adder_1_out));  // open: cin, cout
  Register #(.width(6)) register_1 (.D(adder_1_out), .Q(register_1_q), .clk(Clock), .clr(Reset));  // open: en
  RAM #(.addrWidth(6), .dataWidth(16), .Datafile_on_reset("C:\\Users\\sebto\\Dropbox\\Sebastián\\Estudios\\Tecnología de computadores\\Topic 3\\Memory")) ram_1 (
    .addr(register_1_q), .data(Current_Instruction));  // open: sel, clk, ld, clr
endmodule
