// Logisim project decoder (1).circ as structural Verilog: 1 circuit, main circuit main
module main (
  input  [15:0] in_1,
  output [2:0] opc
);


  assign opc = in_1[15:13];

  // Notes on the sheet:
  //   addr
  //   imm
  //   func
  //   rs
  //   rd
endmodule
