// Logisim project memory_element.circ as structural Verilog: 2 circuits, main circuit main
module main (
  input  [7:0] Imput,
  input  Load,
  input  [5:0] Address,
  output [7:0] out_4
);

  wire clock_1_out;

  Clock clock_1 (.out(clock_1_out));
  memory_element memory_element_1 (.imput(Imput), .load(Load), .adress(Address), .clock(clock_1_out), .out_5(out_4));
endmodule

module memory_element (
  input  [7:0] imput,
  input  load,
  input  [5:0] adress,
  input  clock,
  output [7:0] out_5
);

  wire not_1_out;

  assign out_5 = load ? imput : 8'bz;  // Controlled_Buffer controlled_buffer_1
  not not_1 (not_1_out, load);
  RAM #(.addrWidth(6)) ram_1 (.addr(adress), .data(out_5), .clk(clock), .ld(not_1_out));  // open: sel, clr
endmodule
