// Logisim project Z23.circ as structural Verilog: 7 circuits, main circuit main
// RW
module main (
  input  in_1,
  output [7:0] Output,
  output [7:0] OUT,
  output [7:0] R_rs,
  output [7:0] R_rd
);

  wire and_1_out, and_2_out, CLK, halt, imty, MW, not_1_out, rd, rs, Rsource, RW;
  wire [2:0] decoder_1_opc, func;
  wire [5:0] addr;
  wire [7:0] imm, mem_output, MemInput, multiplexer_2_out, r0_q, r1_q, RegInput, register_r_rs;
  wire [15:0] instructionmemory_1_current_instruction;

  register register (.in_1(RegInput), .rs(rs), .rd(rd), .RW(RW), .clk(CLK), .R_rs(register_r_rs), .R_rd(MemInput));
  ALU ALU (.func(func), .A(register_r_rs), .B(multiplexer_2_out), .OUT(OUT));
  memory mem (.Input(MemInput), .Write(MW), .Address(addr), .Clock(CLK), .Output(mem_output));
  Multiplexer #(.width(8), .enable("false")) multiplexer_1 (.in0(OUT), .in1(mem_output), .out(RegInput), .sel(Rsource));
  Multiplexer #(.width(8), .enable("false")) multiplexer_2 (
    .in0(MemInput), .in1(imm), .out(multiplexer_2_out), .sel(imty));
  Register r0 (.D(RegInput), .en(and_1_out), .Q(r0_q), .clk(CLK));  // open: clr
  and and_1 (and_1_out, ~rd, RW);  // AND_Gate
  Register r1 (.D(RegInput), .en(and_2_out), .Q(r1_q), .clk(CLK));  // open: clr
  and and_2 (and_2_out, rd, RW);
  Clock clock_1 (.out(CLK));
  Multiplexer #(.width(8), .enable("false")) multiplexer_3 (.in0(r0_q), .in1(r1_q), .out(R_rs), .sel(rs));
  assign Output = MW ? MemInput : 8'bz;  // Controlled_Buffer controlled_buffer_1
  // Probe on instructionmemory_1_current_instruction
  InstructionMemory instructionmemory_1 (
    .Clock(CLK), .Reset(in_1), .Current_Instruction(instructionmemory_1_current_instruction));
  Multiplexer #(.width(8), .enable("false")) multiplexer_4 (.in0(r0_q), .in1(r1_q), .out(R_rd), .sel(rd));
  not not_1 (not_1_out, MW);
  Decoder decoder_1 (
    .instruction(instructionmemory_1_current_instruction), .addr(addr), .imm(imm), .func(func), .rs(rs),
    .rd(rd), .opc(decoder_1_opc));
  CU cu_1 (.in_1(decoder_1_opc), .MW(MW), .Rsource(Rsource), .RW(RW), .imty(imty), .halt(halt));
  RAM #(.addrWidth(6)) ram_1 (.addr(addr), .data(Output), .clk(CLK), .ld(not_1_out));  // open: sel, clr

  // Notes on the sheet:
  //   REGISTRY
  //   MEMORY
endmodule

module register (
  input  [7:0] in_1,
  input  rs,
  input  rd,
  input  RW,
  input  clk,
  output [7:0] R_rs,
  output [7:0] R_rd
);

  wire and_1_out, and_2_out;
  wire [7:0] r0_q, r1_q;

  Register r0 (.D(in_1), .en(and_1_out), .Q(r0_q), .clk(clk));  // open: clr
  and and_1 (and_1_out, ~rd, RW);  // AND_Gate
  Register r1 (.D(in_1), .en(and_2_out), .Q(r1_q), .clk(clk));  // open: clr
  and and_2 (and_2_out, rd, RW);
  Multiplexer #(.width(8), .enable("false")) multiplexer_1 (.in0(r0_q), .in1(r1_q), .out(R_rs), .sel(rs));
  Multiplexer #(.width(8), .enable("false")) multiplexer_2 (.in0(r0_q), .in1(r1_q), .out(R_rd), .sel(rd));
endmodule

module memory (
  input  [7:0] Input,
  input  Write,
  input  [5:0] Address,
  input  Clock,
  output [7:0] Output
);

  wire not_1_out;

  assign Output = Write ? Input : 8'bz;  // Controlled_Buffer controlled_buffer_1
  not not_1 (not_1_out, Write);
  RAM #(.addrWidth(6)) ram_1 (.addr(Address), .data(Output), .clk(Clock), .ld(not_1_out));  // open: sel, clr
endmodule

module ALU (
  input  [7:0] A,
  input  [7:0] B,
  input  [2:0] func,
  output [7:0] OUT
);

  wire bitselector_1_out, bitselector_2_out, comparator_1_lt, xor_1_out;
  wire [7:0] adder_1_out, bit_extender_3_out, bit_extender_4_out, multiplexer_1_out, multiplier_1_out,
       subtractor_1_out;
  wire [8:0] bit_extender_1_out, bit_extender_2_out, divider_1_out, divider_1_rem, multiplexer_3_out,
       multiplexer_4_out, multiplexer_5_out, multiplexer_6_out, negator_1_out, negator_2_out, negator_3_out,
       negator_4_out;

  Adder adder_1 (.a(A), .b(B), .out(adder_1_out));  // open: cin, cout
  Subtractor subtractor_1 (.a(A), .b(B), .out(subtractor_1_out));  // open: bin, bout
  Multiplier multiplier_1 (.a(A), .b(B), .out(multiplier_1_out));  // open: cin, cout
  Comparator comparator_1 (.a(A), .b(B), .lt(comparator_1_lt));  // open: gt, eq
  Multiplexer #(.width(8), .enable("false")) multiplexer_1 (
    .in0(B), .in1(A), .out(multiplexer_1_out), .sel(comparator_1_lt));
  Multiplexer #(.select(3), .width(8), .enable("false")) multiplexer_2 (
    .in0(A), .in1(B), .in2(adder_1_out), .in3(subtractor_1_out), .in4(multiplier_1_out),
    .in5(bit_extender_3_out), .in6(bit_extender_4_out), .in7(multiplexer_1_out), .out(OUT), .sel(func));
  Negator #(.width(9)) negator_1 (.in(bit_extender_1_out), .out(negator_1_out));
  assign bit_extender_1_out = {{1{A[7]}}, A};  // Bit_Extender bit_extender_1
  assign bit_extender_2_out = {{1{B[7]}}, B};  // Bit_Extender bit_extender_2
  Negator #(.width(9)) negator_2 (.in(bit_extender_2_out), .out(negator_2_out));
  Multiplexer #(.width(9), .enable("false")) multiplexer_3 (
    .in0(bit_extender_1_out), .in1(negator_1_out), .out(multiplexer_3_out), .sel(bitselector_1_out));
  Multiplexer #(.width(9), .enable("false")) multiplexer_4 (
    .in0(bit_extender_2_out), .in1(negator_2_out), .out(multiplexer_4_out), .sel(bitselector_2_out));
  BitSelector bitselector_1 (.in(A), .out(bitselector_1_out), .sel(3'b111));
  BitSelector bitselector_2 (.in(B), .out(bitselector_2_out), .sel(3'b111));
  Divider #(.width(9)) divider_1 (
    .a(multiplexer_3_out), .b(multiplexer_4_out), .out(divider_1_out), .rem(divider_1_rem));  // open: upper
  xor xor_1 (xor_1_out, bitselector_1_out, bitselector_2_out);
  Negator #(.width(9)) negator_3 (.in(divider_1_out), .out(negator_3_out));
  Negator #(.width(9)) negator_4 (.in(divider_1_rem), .out(negator_4_out));
  Bit_Extender #(.in_width(9), .out_width(8), .\type ("sign")) bit_extender_3 (
    .in(multiplexer_5_out), .out(bit_extender_3_out));
  Multiplexer #(.width(9), .enable("false")) multiplexer_5 (
    .in0(divider_1_out), .in1(negator_3_out), .out(multiplexer_5_out), .sel(xor_1_out));
  Multiplexer #(.width(9), .enable("false")) multiplexer_6 (
    .in0(divider_1_rem), .in1(negator_4_out), .out(multiplexer_6_out), .sel(bitselector_1_out));
  Bit_Extender #(.in_width(9), .out_width(8), .\type ("sign")) bit_extender_4 (
    .in(multiplexer_6_out), .out(bit_extender_4_out));
endmodule

module InstructionMemory (
  input  Clock,
  input  Reset,
  output [15:0] Current_Instruction
);

  wire [5:0] adder_1_out, register_1_q;

  Adder #(.width(6)) adder_1 (.a(register_1_q), .b(6'b000001), .out(adder_1_out));  // open: cin, cout
  Register #(.width(6)) register_1 (.D(adder_1_out), .Q(register_1_q), .clk(Clock), .clr(Reset));  // open: en
  RAM #(.addrWidth(6), .dataWidth(16), .Datafile_on_reset("C:\\Users\\javie\\OneDrive\\Documentos\\Programming\\Z23Computer\\program")) ram_1 (
    .addr(register_1_q), .data(Current_Instruction));  // open: sel, clk, ld, clr
endmodule

module Decoder (
  input  [15:0] instruction,
  output [5:0] addr,
  output [7:0] imm,
  output [2:0] func,
  output rs,
  output rd,
  output [2:0] opc
);


  assign addr = instruction[5:0];
  assign func = instruction[10:8];
  assign imm = instruction[7:0];
  assign opc = instruction[15:13];
  assign rd = instruction[12];
  assign rs = instruction[11];

  // Notes on the sheet:
  //   addr
  //   imm
  //   func
  //   rs
  //   rd
endmodule

module CU (
  input  [2:0] in_1,
  output MW,
  output Rsource,
  output RW,
  output imty,
  output halt
);

  wire demultiplexer_1_out2;

  Demultiplexer #(.select(3), .disabled(0), .enable("false")) demultiplexer_1 (
    .out0(MW), .out1(imty), .out2(demultiplexer_1_out2), .out3(Rsource), .out7(halt), .in(1'b1), .sel(in_1));  // open: out4, out5, out6
  or or_1 (RW, imty, demultiplexer_1_out2, Rsource);
endmodule
