// Logisim project circuit.circ as structural Verilog: 4 circuits, main circuit main
// RW
module main (
  output [7:0] OUT
);

  wire [7:0] mem_output, multiplexer_1_out, multiplexer_2_out, register_r_rd, register_r_rs;

  register register (.in_1(multiplexer_1_out), .R_rs(register_r_rs), .R_rd(register_r_rd));  // open: rs, rd, RW, clk
  ALU ALU (.A(register_r_rs), .B(multiplexer_2_out), .OUT(OUT));  // open: func
  memory mem (.Input(register_r_rd), .Output(mem_output));  // open: Write, Address, Clock
  Multiplexer #(.width(8)) multiplexer_1 (.in0(OUT), .in1(mem_output), .out(multiplexer_1_out));  // open: sel, en
  Multiplexer #(.width(8)) multiplexer_2 (
    .in0(register_r_rd), .in1({8{1'b1}}), .out(multiplexer_2_out));  // open: sel, en
endmodule

module register (
  input  [7:0] in_1,
  input  rs,
  input  rd,
  input  RW,
  input  clk,
  output [7:0] R_rs,
  output [7:0] R_rd
);

  wire and_1_out, and_2_out;
  wire [7:0] r0_q, r1_q;

  Register r0 (.D(in_1), .en(and_1_out), .Q(r0_q), .clk(clk));  // open: clr
  and and_1 (and_1_out, ~rd, RW);  // AND_Gate
  Register r1 (.D(in_1), .en(and_2_out), .Q(r1_q), .clk(clk));  // open: clr
  and and_2 (and_2_out, rd, RW);
  Multiplexer #(.width(8), .enable("false")) multiplexer_1 (.in0(r0_q), .in1(r1_q), .out(R_rs), .sel(rs));
  Multiplexer #(.width(8), .enable("false")) multiplexer_2 (.in0(r0_q), .in1(r1_q), .out(R_rd), .sel(rd));
endmodule

module memory (
  input  [7:0] Input,
  input  Write,
  input  [3:0] Address,
  input  Clock,
  output [7:0] Output
);

  wire not_1_out;

  assign Output = Write ? Input : 8'bz;  // Controlled_Buffer controlled_buffer_1
  not not_1 (not_1_out, Write);
  RAM #(.addrWidth(4)) ram_1 (.addr(Address), .data(Output), .clk(Clock), .ld(not_1_out));  // open: sel, clr
endmodule

module ALU (
  input  [7:0] A,
  input  [7:0] B,
  input  [2:0] func,
  output [7:0] OUT
);

  wire bitselector_1_out, bitselector_2_out, comparator_1_lt, xor_1_out;
  wire [7:0] adder_1_out, bit_extender_3_out, bit_extender_4_out, multiplexer_1_out, multiplier_1_out,
       subtractor_1_out;
  wire [8:0] bit_extender_1_out, bit_extender_2_out, divider_1_out, divider_1_rem, multiplexer_3_out,
       multiplexer_4_out, multiplexer_5_out, multiplexer_6_out, negator_1_out, negator_2_out, negator_3_out,
       negator_4_out;

  Adder adder_1 (.a(A), .b(B), .out(adder_1_out));  // open: cin, cout
  Subtractor subtractor_1 (.a(A), .b(B), .out(subtractor_1_out));  // open: bin, bout
  Multiplier multiplier_1 (.a(A), .b(B), .out(multiplier_1_out));  // open: cin, cout
  Comparator comparator_1 (.a(A), .b(B), .lt(comparator_1_lt));  // open: gt, eq
  Multiplexer #(.width(8), .enable("false")) multiplexer_1 (
    .in0(B), .in1(A), .out(multiplexer_1_out), .sel(comparator_1_lt));
  Multiplexer #(.select(3), .width(8), .enable("false")) multiplexer_2 (
    .in0(A), .in1(B), .in2(adder_1_out), .in3(subtractor_1_out), .in4(multiplier_1_out),
    .in5(bit_extender_3_out), .in6(bit_extender_4_out), .in7(multiplexer_1_out), .out(OUT), .sel(func));
  Negator #(.width(9)) negator_1 (.in(bit_extender_1_out), .out(negator_1_out));
  assign bit_extender_1_out = {{1{A[7]}}, A};  // Bit_Extender bit_extender_1
  Negator #(.width(9)) negator_2 (.in(bit_extender_2_out), .out(negator_2_out));
  assign bit_extender_2_out = {{1{B[7]}}, B};  // Bit_Extender bit_extender_2
  Multiplexer #(.width(9), .enable("false")) multiplexer_3 (
    .in0(bit_extender_1_out), .in1(negator_1_out), .out(multiplexer_3_out), .sel(bitselector_2_out));
  Multiplexer #(.width(9), .enable("false")) multiplexer_4 (
    .in0(bit_extender_2_out), .in1(negator_2_out), .out(multiplexer_4_out), .sel(bitselector_1_out));
  BitSelector bitselector_1 (.in(B), .out(bitselector_1_out), .sel(3'b111));
  BitSelector bitselector_2 (.in(A), .out(bitselector_2_out), .sel(3'b111));
  Divider #(.width(9)) divider_1 (
    .a(multiplexer_3_out), .b(multiplexer_4_out), .out(divider_1_out), .rem(divider_1_rem));  // open: upper
  xor xor_1 (xor_1_out, bitselector_2_out, bitselector_1_out);
  Negator #(.width(9)) negator_3 (.in(divider_1_out), .out(negator_3_out));
  Negator #(.width(9)) negator_4 (.in(divider_1_rem), .out(negator_4_out));
  Bit_Extender #(.in_width(9), .out_width(8), .\type ("sign")) bit_extender_3 (
    .in(multiplexer_5_out), .out(bit_extender_3_out));
  Multiplexer #(.width(9), .enable("false")) multiplexer_5 (
    .in0(divider_1_out), .in1(negator_3_out), .out(multiplexer_5_out), .sel(xor_1_out));
  Bit_Extender #(.in_width(9), .out_width(8), .\type ("sign")) bit_extender_4 (
    .in(multiplexer_6_out), .out(bit_extender_4_out));
  Multiplexer #(.width(9), .enable("false")) multiplexer_6 (
    .in0(divider_1_rem), .in1(negator_4_out), .out(multiplexer_6_out), .sel(bitselector_2_out));
endmodule
